# Fritzing sketch esp-media-control (saved by Fritzing 0.9.5d)

parts:
  M1 = ESP32-S3-DevKitC-1-N8R8-v1 [part_number=ESP32-S3-DevKitC-1-N8R8-v1]
  U1 = POT [package=pot_alpha_rv16af-20]
  S1 = Pushbutton [package="[SMD]"]
  C1 = Ceramic Capacitor [capacitance="100 nF" package="0603 [SMD, multilayer]"]
  S3 = Pushbutton [package="[SMD]"]
  S2 = Pushbutton [package="[SMD]"]
  J1 = single row smd male pin header, 5 pins [form="♂ (male)"]
  J2 = single row smd male pin header, 3 pins [form="♂ (male)"]
  J3 = single row smd male pin header, 3 pins [form="♂ (male)"]

nets:
  N1: M1.pin_1, M1.pin_2, U1.A
  N2: M1.pin_16, S1.Pin_3, S1.Pin_4
  N3: M1.pin_17, S2.Pin_3, S2.Pin_4
  N4: M1.pin_18, S3.Pin_3, S3.Pin_4
  N5: M1.pin_22, M1.pin_44, J1.pin1
  N6: M1.pin_41, J2.pin2
  N7: U1.S, J2.pin1
  N8: U1.E, J3.pin1
  N9: S1.Pin_1, S1.Pin_2, J1.pin5
  N10: C1.0, J3.pin3
  N11: C1.1, J2.pin3
  N12: S3.Pin_1, S3.Pin_2, J1.pin3
  N13: S2.Pin_1, S2.Pin_2, J1.pin4
  N14: J1.pin2, J3.pin2

custom parts:
  ESP32-S3-DevKitC-1-N8R8-v1: ESP32-S3-DevKitC-1-N8R8-v1 This module is 44pins long (2x22) and 11 pins width.
